// Logisim project EXPLICAÇÃO.circ as structural Verilog: 1 circuit, main circuit main
module main (
  input  A,
  input  B,
  input  C,
  input  D,
  input  A_2,
  input  B_2,
  input  C_2,
  input  D_2,
  input  A_3,
  input  B_3,
  input  C_3,
  input  D_3,
  input  B_4,
  input  A_4,
  input  C_4,
  input  D_4,
  output out_17,
  output out_18,
  output out_19,
  output out_20
);

  wire and_1_out, and_2_out, and_3_out, and_4_out, and_5_out, nand_1_out, nand_2_out, nand_3_out, nand_4_out,
       nand_5_out, nand_7_out, nand_8_out, nand_9_out, or_1_out, or_2_out;

  nand nand_1 (nand_1_out, B_4, A_4);
  nand nand_2 (nand_2_out, A_4, C_4);
  nand nand_3 (nand_3_out, B_4, C_4, D_4);
  and and_1 (and_1_out, C, D);
  or or_1 (or_1_out, B_2, C_2);
  and and_2 (and_2_out, B_2, C_2, D_2);
  nand nand_4 (nand_4_out, C_3, D_3);
  or or_2 (or_2_out, A, and_1_out);
  and and_3 (and_3_out, A_2, or_1_out);
  nand nand_5 (nand_5_out, A_3, A_3);
  nand nand_6 (out_20, nand_1_out, nand_2_out, nand_3_out);
  and and_4 (and_4_out, A, C);
  or or_3 (out_18, and_3_out, and_2_out);
  nand nand_7 (nand_7_out, nand_5_out, nand_4_out);
  and and_5 (and_5_out, B, or_2_out);
  nand nand_8 (nand_8_out, A_3, C_3);
  or or_4 (out_17, and_4_out, and_5_out);
  nand nand_9 (nand_9_out, B_3, nand_7_out);
  nand nand_10 (out_19, nand_8_out, nand_9_out);

  // Notes on the sheet:
  //   TIAGO
  //   AULA 4 [CIRCUITO]
  //   TIAGO
  //   CONVERSÃO PARA NAND [JOÃO]
  //   JOÃO
  //   A*C+B(A+C*D)
  //   A(B+C) + (B*C*D)
endmodule
