// Logisim project TESTE.circ as structural Verilog: 1 circuit, main circuit main
module main (
  input  in_1,
  input  in_2,
  input  in_3,
  input  in_4,
  input  in_5,
  input  in_6,
  input  in_7,
  input  in_8,
  input  in_9,
  input  in_10,
  input  in_11,
  input  in_12,
  input  in_13,
  input  in_14,
  input  in_15,
  input  R,
  input  I,
  input  C,
  input  I_2,
  input  R_2,
  input  C_2,
  output out_22,
  output out_23,
  output out_24,
  output out_25,
  output out_26,
  output out_27,
  output out_28
);

  wire and_1_out, and_2_out, nand_1_out, nand_2_out, nand_3_out, nand_4_out, nand_5_out, nand_6_out,
       nand_7_out, nand_8_out, nand_11_out, nor_1_out, nor_2_out, nor_3_out, nor_4_out, nor_5_out, nor_6_out,
       nor_7_out, nor_8_out, nor_9_out, nor_10_out, nor_11_out, nor_12_out, nor_13_out, nor_14_out,
       nor_15_out, or_1_out;

  nand nand_1 (nand_1_out, in_2, in_2);
  nand nand_2 (nand_2_out, in_3, in_3);
  nand nand_3 (nand_3_out, in_7, in_7);
  nand nand_4 (nand_4_out, in_8, in_9);
  nor nor_1 (nor_1_out, in_11, in_11);
  nor nor_2 (nor_2_out, in_12, in_12);
  nor nor_3 (nor_3_out, in_14, in_14);
  nor nor_4 (nor_4_out, in_15, in_15);
  nor nor_5 (nor_5_out, I_2, I_2);
  nor nor_6 (nor_6_out, R_2, C_2);
  nor nor_7 (nor_7_out, R_2, R_2);
  nor nor_8 (nor_8_out, C_2, C_2);
  or or_1 (or_1_out, in_4, in_5);
  and and_1 (and_1_out, in_4, in_5);
  nand nand_5 (nand_5_out, R, I);
  nand nand_6 (nand_6_out, I, C);
  nand nand_7 (nand_7_out, R, C);
  nand nand_8 (nand_8_out, nand_1_out, nand_2_out);
  and and_2 (and_2_out, or_1_out, in_6);
  nand nand_9 (out_24, nand_3_out, nand_3_out, nand_4_out);
  nor nor_9 (nor_9_out, nor_1_out, nor_2_out);
  nor nor_10 (nor_10_out, nor_3_out, nor_4_out);
  nand nand_10 (out_27, nand_5_out, nand_6_out, nand_7_out);
  nor nor_11 (nor_11_out, nor_5_out, nor_6_out);
  nor nor_12 (nor_12_out, nor_7_out, nor_8_out);
  nand nand_11 (nand_11_out, in_1, nand_8_out);
  nor nor_13 (nor_13_out, in_10, nor_9_out);
  nor nor_14 (nor_14_out, in_13, nor_10_out);
  or or_2 (out_23, and_2_out, and_1_out);
  nor nor_15 (nor_15_out, nor_11_out, nor_12_out);
  nand nand_12 (out_22, nand_11_out, nand_11_out, nand_11_out);
  nor nor_16 (out_25, nor_13_out, nor_13_out, nor_13_out);
  nor nor_17 (out_26, nor_14_out, nor_14_out, nor_14_out);
  nor nor_18 (out_28, nor_15_out, nor_15_out, nor_15_out);

  // Notes on the sheet:
  //   CONDIÇÕES:
endmodule
