// Logisim project TP1_P306.circ as structural Verilog: 1 circuit, main circuit main
module main (
  input  D,
  input  C,
  input  I,
  input  S,
  input  D_2,
  input  C_2,
  input  I_2,
  input  S_2,
  output out_9,
  output out_10
);

  wire nand_1_out, nand_2_out, nand_3_out, nand_4_out, nor_1_out, nor_2_out, nor_3_out, nor_4_out, nor_5_out;

  nand nand_1 (nand_1_out, C, C);
  nand nand_2 (nand_2_out, I, S);
  nor nor_1 (nor_1_out, D_2, D_2);
  nor nor_2 (nor_2_out, I_2, I_2);
  nor nor_3 (nor_3_out, S_2, S_2);
  nor nor_4 (nor_4_out, nor_2_out, nor_3_out);
  nand nand_3 (nand_3_out, nand_1_out, nand_2_out);
  nand nand_4 (nand_4_out, D, nand_3_out);
  nor nor_5 (nor_5_out, C_2, nor_4_out);
  nand nand_5 (out_9, nand_4_out, nand_4_out);
  nor nor_6 (out_10, nor_1_out, nor_5_out);

  // Notes on the sheet:
  //   Conversão para NAND
  //   Conversão para NOR
endmodule
