// Logisim project TP2_P308.circ as structural Verilog: 1 circuit, main circuit main
module main (
  input  [3:0] JOGADOR_2,
  input  in_2,
  input  [1:0] MODO,
  input  [3:0] JOGADOR_1,
  input  [3:0] \JOGOS_DA_MÃO ,
  output [3:0] \Nº_SECRETO 
);

  wire and_1_out, and_2_out, button_1_out, comparator_1_eq, comparator_2_eq, comparator_3_eq,
       comparator_4_eq, comparator_4_gt, comparator_4_lt, multiplexer_1_out, not_1_out, not_2_out, not_3_out,
       or_1_out;
  wire [3:0] counter_1_q, counter_2_q, counter_3_q;

  Clock clock_1 ();  // open: out
  not not_1 (not_1_out, comparator_1_eq);
  LED led_1 (.in(comparator_1_eq));
  and and_1 (and_1_out, in_2, not_1_out);
  Random #(.width(4)) random_1 (.clk(and_1_out), .out(\Nº_SECRETO ));  // open: next, clr
  not not_2 (not_2_out, and_1_out);
  LED led_2 (.in(and_1_out));
  Counter #(.width(4), .max('hf)) counter_1 (
    .Q(counter_1_q), .clk(not_2_out), .clr(button_1_out));  // open: load, D, count, carry
  Comparator #(.width(4)) comparator_1 (.a(\JOGOS_DA_MÃO ), .b(counter_1_q), .eq(comparator_1_eq));  // open: gt, lt
  Hex_Digit_Display hex_digit_display_1 (.value(counter_1_q));  // open: dp
  Hex_Digit_Display hex_digit_display_2 (.value(counter_2_q));  // open: dp
  Counter #(.width(4), .max('hf)) counter_2 (
    .count(not_3_out), .Q(counter_2_q), .clk(not_2_out), .clr(button_1_out));  // open: load, D, carry
  not not_3 (not_3_out, multiplexer_1_out);
  Comparator #(.width(4)) comparator_2 (.a(JOGADOR_2), .b(\Nº_SECRETO ), .eq(comparator_2_eq));  // open: gt, lt
  Comparator #(.width(4)) comparator_3 (.a(JOGADOR_1), .b(\Nº_SECRETO ), .eq(comparator_3_eq));  // open: gt, lt
  Counter #(.width(4), .max('hf)) counter_3 (
    .count(multiplexer_1_out), .Q(counter_3_q), .clk(not_2_out), .clr(button_1_out));  // open: load, D, carry
  and and_2 (and_2_out, comparator_2_eq, comparator_3_eq);
  or or_1 (or_1_out, comparator_2_eq, comparator_3_eq);
  Hex_Digit_Display hex_digit_display_3 (.value(counter_3_q));  // open: dp
  Multiplexer #(.select(2)) multiplexer_1 (
    .in0(comparator_2_eq), .in1(comparator_3_eq), .in2(and_2_out), .in3(or_1_out), .out(multiplexer_1_out),
    .sel(MODO));  // open: en
  Comparator #(.width(4)) comparator_4 (
    .a(counter_2_q), .b(counter_3_q), .gt(comparator_4_gt), .eq(comparator_4_eq), .lt(comparator_4_lt));
  Button button_1 (.out(button_1_out));
  LED led_3 (.in(comparator_4_gt));
  LED led_4 (.in(comparator_4_eq));
  LED led_5 (.in(comparator_4_lt));

  // Notes on the sheet:
  //   Fim do Jogo
  //   1 a 15
  //   JOGAR
  //   TENTATIVAS
  //   FALHAS
  //   CONFORME A EXPLICAÇÃO DO PROFESSOR, QUE REFERIU QUE O BOTÃO RECOMEÇAR, RECOMEÇAVA AS FALHAS, OS ACERTOS E TAMBÉM O JOGO.
  //   ACERTOS
  //   MODO:
  //   00- Acertar J2
  //   01- Acertar J1
  //   10- Acertarem Ambos
  //   11- Acertar somente um
  //   RECOMEÇAR
  //   PERDIDA
  //   NULA
  //   GANHA
  //   ______________
endmodule
